# Fritzing sketch PomodoroArduino (saved by Fritzing 0.8.5b)
breadboards: 1

parts:
  Part1 = Arduino Uno (Rev3)
  S1 = Pushbutton [package="[THT]"]
  S2 = Pushbutton [package="[THT]"]
  S3 = Pushbutton [package="[THT]"]
  J1 = Piezo Speaker
  J2 = Basic Servo
  C1 = Electrolytic Capacitor [capacitance=1µF package="100 mil [THT, electrolytic]"]
  LED1 = LED - 5mm [color="Red (633nm)" package="5 mm [THT]"]
  LED2 = LED - 5mm [color="Red (633nm)" package="5 mm [THT]"]
  LED3 = LED - 5mm [color="Red (633nm)" package="5 mm [THT]"]
  R1 = Resistor [tolerance=±5% resistance=220 package=THT]
  R2 = Resistor [tolerance=±5% resistance=220 package=THT]
  R3 = Resistor [tolerance=±5% resistance=220 package=THT]

nets:
  N1: Part1.D9_PWM, J2.pulse
  N2: Part1.D11_PWM/MOSI, J1.pin2
  GND: Part1.GND, S1.Pin_3, S1.Pin_4, S2.Pin_3, S2.Pin_4, S3.Pin_3, S3.Pin_4, J1.pin1, J2.gnd, C1.-, R1.Pin_1, R2.Pin_1, R3.Pin_1
  N3: Part1.D2, S3.Pin_1, S3.Pin_2
  N4: Part1.D3_PWM, S2.Pin_1, S2.Pin_2
  N5: Part1.D4, S1.Pin_1, S1.Pin_2
  N6: Part1.D5_PWM, LED1.anode
  N7: Part1.D6_PWM, LED2.anode
  N8: Part1.D7, LED3.anode
  5V: Part1.5V, J2.vcc, C1.+
  N9: LED1.cathode, R1.Pin_0
  N10: LED2.cathode, R2.Pin_0
  N11: LED3.cathode, R3.Pin_0
