# Fritzing sketch PomodoroArduino (saved by Fritzing 0.8.3b)
breadboards: 1

parts:
  Part1 = Arduino Pro Mini v13
  LED1 = LED - 5mm [color="Red (633nm)" package="5 mm [THT]"]
  LED2 = LED - 5mm [color="Green (555nm)" package="5 mm [THT]"]
  LED3 = LED - 5mm [color="Blue (470nm)" package="5 mm [THT]"]
  S1 = Pushbutton [package="[THT]"]
  S2 = Pushbutton [package="[THT]"]
  S3 = Pushbutton [package="[THT]"]
  J1 = Piezo Speaker
  MOTOR1 = Vibration Motor
  J2 = Screw terminal - 2 pins [package=THT]
  R1 = Resistor [tolerance=±5% resistance=220 package=THT]
  R2 = Resistor [tolerance=±5% resistance=220 package=THT]
  R3 = Resistor [tolerance=±5% resistance=220 package=THT]

nets:
  N1: Part1.VCC, J2.pin2
  GND: Part1.GND, S1.Pin_3, S1.Pin_4, S2.Pin_3, S2.Pin_4, S3.Pin_3, S3.Pin_4, J1.pin1, MOTOR1.NEG, J2.pin1, R1.Pin_1, R2.Pin_1, R3.Pin_1
  N2: Part1.D11_PWM/MOSI, J1.pin2
  N3: Part1.D10_PWM/SS, MOTOR1.POS
  N4: Part1.D9_PWM, LED3.anode
  N5: Part1.D8, S3.Pin_1, S3.Pin_2
  N6: Part1.D7, S2.Pin_1, S2.Pin_2
  N7: Part1.D6_PWM, LED2.anode
  N8: Part1.D5_PWM, LED1.anode
  N9: Part1.D4, S1.Pin_1, S1.Pin_2
  N10: LED1.cathode, R2.Pin_0
  N11: LED2.cathode, R3.Pin_0
  N12: LED3.cathode, R1.Pin_0

custom parts:
  Vibration Motor: An eccentric vibration motor!
